# Fritzing sketch banners (saved by Fritzing 1.0.3b)
circuit board: 4.99999cm x 10cm
breadboards: 2

parts:
  S11 = SPST Switch [package=switch-spdt_kit]
  Power_plug2 = Power plug
  4001 = Rectifier Diode [part_number=1N4001 package="300 mil [THT]"]
  100uF = Electrolytic Capacitor [capacitance=0.1mF voltage=35V package="100 mil [THT, electrolytic]"]
  100uF1 = Electrolytic Capacitor [capacitance=0.1mF voltage=35V package="100 mil [THT, electrolytic]"]
  104 = Ceramic Capacitor [capacitance=100nF voltage=16V package="200 mil [THT, multilayer]"]
  -G = double row female pin header, 4 pins [form="♀ (female)"]
  J4 = double row female pin header, 2 pins [form="♀ (female)"]
  input = double row female pin header, 4 pins [form="♀ (female)"]
  LDR = double row female pin header, 4 pins [form="♀ (female)"]
  LED4 = LED - 3mm [color="Red (635nm)" current=0.030A package="3 mm [THT]"]
  1K1 = Resistor [tolerance=±5% resistance=1k power=0.25W package=THT]
  LDR1 = Photocell (LDR) [power=0.25W dark_resistance_@0.01lx=300kΩ light_resistance_@100lx=400Ω luminance=10lx package=THT]
  LED = female pin header, 2 pins [form="♀ (female)"]
  100K = Rotary Potentiometer (Small) [maximum_resistance=100kΩ knob_status=50% power=0.5W package=THT]
  100K_2 = Rotary Potentiometer (Small) [maximum_resistance=100kΩ knob_status=50% power=0.5W package=THT]
  100K_3 = Rotary Potentiometer (Small) [maximum_resistance=100kΩ knob_status=50% power=0.5W package=THT]
  100K_4 = Rotary Potentiometer (Small) [maximum_resistance=100kΩ knob_status=50% power=0.5W package=THT]
  out = Audio Jack (TRS) 3.5mm [package="PG203J [THT]"]
  out_2 = double row female pin header, 2 pins [form="♀ (female)"]
  sw2 = SPST Switch [package=switch-spdt_kit]
  sw1 = SPST Switch [package=switch-spdt_kit]
  sw1_2 = female pin header, 2 pins [form="♀ (female)"]
  sw2_2 = female pin header, 2 pins [form="♀ (female)"]
  LED2 = female pin header, 2 pins [form="♀ (female)"]
  LED6 = LED - 3mm [color="Red (635nm)" current=0.030A package="3 mm [THT]"]
  1K2 = Resistor [tolerance=±5% resistance=1k power=0.25W package=THT]
  LDR2 = double row female pin header, 4 pins [form="♀ (female)"]
  LDR3 = Photocell (LDR) [power=0.25W dark_resistance_@0.01lx=300kΩ light_resistance_@100lx=400Ω luminance=10lx package=THT]
  LED7 = female pin header, 1 pin [form="♀ (female)"]
  LED8 = female pin header, 1 pin [form="♀ (female)"]
  LED9 = female pin header, 1 pin [form="♀ (female)"]
  l = female pin header, 1 pin [form="♀ (female)"]  # not connected
  +v = double row female pin header, 4 pins [form="♀ (female)"]
  Input = Audio Jack (TRS) 3.5mm [package="PG203J [THT]"]
  IC1 = TL074 Quad Opamp (Movable) [package="DIP (Dual Inline)"]  # not connected
  IC1_PWR = TL074 Quad Opamp (Movable) [package="DIP (Dual Inline)"]  # not connected
  IC1_A = TL074 Quad Opamp (Movable) [package="DIP (Dual Inline)"]  # not connected
  IC1_B = TL074 Quad Opamp (Movable) [package="DIP (Dual Inline)"]  # not connected
  IC1_C = TL074 Quad Opamp (Movable) [package="DIP (Dual Inline)"]  # not connected
  IC1_D = TL074 Quad Opamp (Movable) [package="DIP (Dual Inline)"]  # not connected
  IC2 = TL074 Quad Opamp (Movable) [package="DIP (Dual Inline)"]
  IC2_PWR = TL074 Quad Opamp (Movable) [package="DIP (Dual Inline)"]  # not connected
  IC2_A = TL074 Quad Opamp (Movable) [package="DIP (Dual Inline)"]  # not connected
  IC2_B = TL074 Quad Opamp (Movable) [package="DIP (Dual Inline)"]  # not connected
  IC2_C = TL074 Quad Opamp (Movable) [package="DIP (Dual Inline)"]  # not connected
  IC2_D = TL074 Quad Opamp (Movable) [package="DIP (Dual Inline)"]  # not connected
  Jm2 = female pin header, 3 pins [form="♀ (female)"]
  Jm6 = female pin header, 3 pins [form="♀ (female)"]
  Jm4 = female pin header, 3 pins [form="♀ (female)"]
  Jm5 = female pin header, 3 pins [form="♀ (female)"]
  47K = Resistor [tolerance=±5% resistance=47k power=0.25W package=THT]

nets:
  N1: S11.O, LED9.pin1
  N2: S11.P, Power_plug2.VCC, J4.pin1
  N3: S11.S, 4001.anode
  GND: Power_plug2.GND, 100uF.-, 100uF1.-, 104.1, -G.pin1, -G.pin2, -G.pin3, -G.pin4, J4.pin2, 1K1.Pin_1, out.Sleeve, out_2.pin1, 1K2.Pin_1, Input.Sleeve
  N4: 4001.cathode, 100uF.+, +v.pin1, +v.pin2, +v.pin3, +v.pin4, IC2.connector9
  N5: 100uF1.+, 104.0
  N6: input.pin1, input.pin2, Input.Tip
  N7: input.pin3, input.pin4, Input.Ring, 47K.Pin_1
  N8: LDR.pin1, LDR.pin2, LDR1.pin_1
  N9: LDR.pin3, LDR.pin4, LDR1.pin_0
  N10: LED4.cathode, 1K1.Pin_0
  N11: LED4.anode, LED.pin1, LED.pin2
  N12: 100K.leg1, Jm2.pin3
  N13: 100K.wiper, Jm2.pin2
  N14: 100K.leg2, Jm2.pin1
  N15: 100K_2.leg1, Jm6.pin3
  N16: 100K_2.wiper, Jm6.pin2
  N17: 100K_2.leg2, Jm6.pin1
  N18: 100K_3.leg1, Jm4.pin3
  N19: 100K_3.wiper, Jm4.pin2
  N20: 100K_3.leg2, Jm4.pin1
  N21: 100K_4.leg1, Jm5.pin3
  N22: 100K_4.wiper, Jm5.pin2
  N23: 100K_4.leg2, Jm5.pin1
  N24: out.Ring, out.Tip, out_2.pin2
  N25: sw2.O, sw2_2.pin1
  N26: sw2.P, sw2_2.pin2
  N27: sw2.S, LED7.pin1
  N28: sw1.O, sw1_2.pin1
  N29: sw1.P, sw1_2.pin2
  N30: sw1.S, LED8.pin1
  N31: LED2.pin1, LED2.pin2, LED6.anode
  N32: LED6.cathode, 1K2.Pin_0
  N33: LDR2.pin1, LDR2.pin2, LDR3.pin_1
  N34: LDR2.pin3, LDR2.pin4, LDR3.pin_0
  N35: IC2.connector1, 47K.Pin_0

notes:
  banners
  blueprint@poetaster.de 2024
  jlcjlcjlcjlc

custom parts:
  TL074 Quad Opamp (Movable): Quadruple Operational Amplifier (Opamp)
  TL074 Quad Opamp (Movable): Quadruple Operational Amplifier (Opamp)
  TL074 Quad Opamp (Movable): Quadruple Operational Amplifier (Opamp)
  TL074 Quad Opamp (Movable): Quadruple Operational Amplifier (Opamp)
  TL074 Quad Opamp (Movable): Quadruple Operational Amplifier (Opamp)
  TL074 Quad Opamp (Movable): Quadruple Operational Amplifier (Opamp)
